# Fritzing sketch KY (saved by Fritzing 0.8.7b)
breadboards: 2

parts:
  元件1 = Arduino Uno (Rev3)
  元件2 = Bluetooth Module Breakout - Roving Networks (RN-41)
  M1 = DC Motor
  M2 = DC Motor
  EDGY_motor_control2 = EDGY
  Servo1 = Basic Servo
  R1 = Resistor [tolerance=±5% resistance=220 package=THT]
  R2 = Resistor [tolerance=±5% resistance=220 package=THT]
  X1 = Sonar
  S1 = Pushbutton [package="[THT]"]
  C1 = Tantalum Capacitor [capacitance=1μF package="100 mil [THT, tantalum]"]

nets:
  N1: 元件1.A3, X1.Emisor
  N2: 元件1.A4/SDA, X1.Receptor
  N3: 元件1.D8, R1.Pin_1, S1.Pin_3, S1.Pin_4
  N4: 元件1.D9_PWM, EDGY_motor_control2.A2
  N5: 元件1.D10_PWM/SS, EDGY_motor_control2.B2
  N6: 元件1.D11_PWM/MOSI, C1.+
  N7: 元件1.D0/RX, 元件2.UARTTX
  N8: 元件1.D1/TX, 元件2.UARTRX
  VCC: 元件1.D3_PWM, 元件1.5V, 元件2.VCC, Servo1.vcc, Servo1.pulse, X1.+5, S1.Pin_1, S1.Pin_2
  N9: 元件1.D5_PWM, EDGY_motor_control2.A1
  N10: 元件1.D6_PWM, EDGY_motor_control2.B1
  GND: 元件1.GND, 元件2.GND, Servo1.gnd, R1.Pin_0, R2.Pin_1, X1.gnd
  N11: M1.pin_1, EDGY_motor_control2.A1out
  N12: M1.pin_2, EDGY_motor_control2.B1out
  N13: M2.pin_1, EDGY_motor_control2.A2out
  N14: M2.pin_2, EDGY_motor_control2.B2out
  N15: R2.Pin_0, C1.-

custom parts:
  Sonar: Devantech SRF08 sonar range-finder. I2C interface. Other Devantech sonars similar
